// Logisim project Circuit_7.19.circ as structural Verilog: 1 circuit, main circuit main
module main (
  input  X1,
  input  X3,
  input  X4,
  input  X2,
  output X1X3X4___X2
);

  wire and_1_out;

  and and_1 (and_1_out, X1, X3, X4);
  or or_1 (X1X3X4___X2, and_1_out, X2);
endmodule
