// Logisim project Circuit_Table_7.9.circ as structural Verilog: 1 circuit, main circuit main
module main (
  input  X1,
  input  X2,
  input  X3,
  input  X4,
  output F_X1_X2_X3_X4
);

  wire and_1_out, and_2_out, and_3_out, and_4_out, and_5_out, and_6_out, and_7_out, and_8_out, and_9_out,
       not_1_out, not_2_out, not_3_out, not_4_out, not_5_out, not_6_out, not_7_out, not_8_out, not_9_out,
       not_10_out, not_11_out, not_12_out, not_13_out;

  not not_1 (not_1_out, X4);
  not not_2 (not_2_out, X3);
  not not_3 (not_3_out, X3);
  not not_4 (not_4_out, X4);
  not not_5 (not_5_out, X2);
  not not_6 (not_6_out, X1);
  not not_7 (not_7_out, X1);
  not not_8 (not_8_out, X4);
  not not_9 (not_9_out, X1);
  not not_10 (not_10_out, X3);
  not not_11 (not_11_out, X1);
  not not_12 (not_12_out, X3);
  not not_13 (not_13_out, X4);
  and and_1 (and_1_out, X1, X2, X3, X4);
  and and_2 (and_2_out, X1, X2, X3, not_1_out);
  and and_3 (and_3_out, X1, X2, not_2_out, X4);
  and and_4 (and_4_out, X1, X2, not_3_out, not_4_out);
  and and_5 (and_5_out, X1, not_5_out, X3, X4);
  and and_6 (and_6_out, not_6_out, X2, X3, X4);
  and and_7 (and_7_out, not_7_out, X2, X3, not_8_out);
  and and_8 (and_8_out, not_9_out, X2, not_10_out, X4);
  and and_9 (and_9_out, not_11_out, X2, not_12_out, not_13_out);
  or or_1 (F_X1_X2_X3_X4, and_1_out, and_2_out, and_3_out, and_4_out, and_5_out, and_6_out, and_7_out, and_8_out, and_9_out);
endmodule
